# Fritzing sketch c2c (saved by Fritzing 0.9.0b)
breadboards: 1

parts:
  Bauteil1 = Arduino Uno (Rev3)
  LED1 = LED - 5mm [color="Red (633nm)" package="5 mm [THT]"]
  R3 = Resistor [tolerance=±5% resistance=10k package=THT]
  R4 = Photocell (LDR) [package=THT]

nets:
  N1: Bauteil1.A0, R3.Pin_1, R4.pin_0
  N2: Bauteil1.D13/SCK, LED1.anode
  N3: Bauteil1.GND, LED1.cathode, R3.Pin_0
  N4: Bauteil1.5V, R4.pin_1
