# Fritzing sketch fritzing-layout (saved by Fritzing 0.8.7b)
breadboards: 1

parts:
  Bauteil1 = Arduino Uno (Rev3)
  LED1 = RGB LED (com. anode, rbg) [package="5 mm [THT]"]
  R1 = Resistor [tolerance=±5% resistance=220 package=THT]
  R2 = Resistor [tolerance=±5% resistance=220 package=THT]
  R3 = Resistor [tolerance=±5% resistance=220 package=THT]

nets:
  N1: Bauteil1.GND, LED1.common_anode
  N2: Bauteil1.D3_PWM, R2.Pin_0
  N3: Bauteil1.D5_PWM, R3.Pin_0
  N4: Bauteil1.D6_PWM, R1.Pin_0
  N5: LED1.red_cathode, R1.Pin_1
  N6: LED1.blue_cathode, R2.Pin_1
  N7: LED1.green_cathode, R3.Pin_1
