# Fritzing sketch c2c (saved by Fritzing 0.8.5b)
breadboards: 1

parts:
  R1 = Photocell (LDR) [package=THT]
  R2 = Resistor [tolerance=±5% resistance=10k package=THT]
  Bauteil1 = Arduino Uno (Rev3)
  LED1 = LED - 5mm [color="Red (633nm)" package="5 mm [THT]"]

nets:
  N1: R1.pin_0, Bauteil1.5V
  N2: R1.pin_1, R2.Pin_0, Bauteil1.A0
  N3: R2.Pin_1, Bauteil1.GND, LED1.cathode
  N4: Bauteil1.D13/SCK, LED1.anode
